# Fritzing sketch 1_Rabbery_Sample (saved by Fritzing 0.9.3b)
breadboards: 1

parts:
  Raspberry_Pi1 = Raspberry Pi B rev2
  LED1 = LED - 5mm [color="Red (633nm)" package="5 mm [THT]"]

nets:
  N1: Raspberry_Pi1.GPIO_27, LED1.cathode
  N2: Raspberry_Pi1.GPIO_11, LED1.anode
