# Fritzing sketch 2_Arudino (saved by Fritzing 0.9.3b)
breadboards: 1

parts:
  LED1 = smd LED [color="Red (633nm)" package="0805 [SMD]"]
  LED2 = smd LED [color="Red (633nm)" package="0805 [SMD]"]
  LED3 = smd LED [color="Red (633nm)" package="0805 [SMD]"]
  LED4 = smd LED [color="Red (633nm)" package="0805 [SMD]"]
  R1 = Resistor [tolerance=±5% resistance=220 package=THT]
  R2 = Resistor [tolerance=±5% resistance=220 package=THT]
  R3 = Resistor [tolerance=±5% resistance=220 package=THT]
  R4 = Resistor [tolerance=±5% resistance=220 package=THT]
  Part1 = Arduino Ethernet Shield (Rev3)
  Part2 = Arduino Board Ethernet  # not connected

nets:
  N1: LED1.cathode, Part1.SDCS
  N2: LED1.anode, R1.Pin_0
  N3: LED2.cathode, Part1.PWM_D5
  N4: LED2.anode, R2.Pin_0
  N5: LED3.cathode, Part1.PWM_D6
  N6: LED3.anode, R3.Pin_0
  N7: LED4.cathode, Part1.D7
  N8: LED4.anode, R4.Pin_0
  N9: R1.Pin_1, R2.Pin_1, R3.Pin_1, R4.Pin_1
